// Logisim project LEC06182018.circ as structural Verilog: 1 circuit, main circuit main
module main (
  input  C_in,
  input  A,
  input  B,
  output out_4
);

  wire A_not, and_1_out, and_2_out, and_3_out, and_4_out, and_5_out, and_6_out, and_7_out, and_8_out, B_not,
       C_in_not, or_1_out, or_2_out;

  not not_1 (A_not, A);
  not not_2 (B_not, B);
  not not_3 (C_in_not, C_in);
  and and_1 (and_1_out, A_not, B_not);
  and and_2 (and_2_out, A_not, B);
  and and_3 (and_3_out, A, B_not);
  and and_4 (and_4_out, A, B);
  and and_5 (and_5_out, and_1_out, C_in);
  and and_6 (and_6_out, and_2_out, C_in_not);
  and and_7 (and_7_out, and_3_out, C_in_not);
  and and_8 (and_8_out, and_4_out, C_in);
  or or_1 (or_1_out, and_5_out, and_6_out);
  or or_2 (or_2_out, and_7_out, and_8_out);
  and and_9 (out_4, or_1_out, or_2_out);
endmodule
