// Logisim project lab08.circ as structural Verilog: 3 circuits, main circuit Multi-Bit ALU
module Multi_Bit_ALU (
  input  [3:0] Operation,
  input  [7:0] A,
  input  [7:0] B,
  output [7:0] Result,
  output Zero,
  output Overflow
);

  wire one_bit_alu_1_carryout, one_bit_alu_2_carryout, one_bit_alu_3_carryout, one_bit_alu_4_carryout,
       one_bit_alu_5_set, one_bit_alu_6_carryout, one_bit_alu_7_carryout, one_bit_alu_8_carryout, or_1_out;

  One_Bit_ALU one_bit_alu_1 (
    .A(A[3]), .B(B[3]), .Less(1'b0), .Ainvert(Operation[3]), .Binvert(Operation[2]),
    .CarryIn(one_bit_alu_8_carryout), .Operation(Operation[1:0]), .CarryOut(one_bit_alu_1_carryout),
    .Result(Result[3]));  // open: Set
  One_Bit_ALU one_bit_alu_2 (
    .A(A[4]), .B(B[4]), .Less(1'b0), .Ainvert(Operation[3]), .Binvert(Operation[2]),
    .CarryIn(one_bit_alu_1_carryout), .Operation(Operation[1:0]), .CarryOut(one_bit_alu_2_carryout),
    .Result(Result[4]));  // open: Set
  One_Bit_ALU one_bit_alu_3 (
    .A(A[5]), .B(B[5]), .Less(1'b0), .Ainvert(Operation[3]), .Binvert(Operation[2]),
    .CarryIn(one_bit_alu_2_carryout), .Operation(Operation[1:0]), .CarryOut(one_bit_alu_3_carryout),
    .Result(Result[5]));  // open: Set
  One_Bit_ALU one_bit_alu_4 (
    .A(A[6]), .B(B[6]), .Less(1'b0), .Ainvert(Operation[3]), .Binvert(Operation[2]),
    .CarryIn(one_bit_alu_3_carryout), .Operation(Operation[1:0]), .CarryOut(one_bit_alu_4_carryout),
    .Result(Result[6]));  // open: Set
  One_Bit_ALU one_bit_alu_5 (
    .A(A[7]), .B(B[7]), .Less(1'b0), .Ainvert(Operation[3]), .Binvert(Operation[2]),
    .CarryIn(one_bit_alu_4_carryout), .Operation(Operation[1:0]), .CarryOut(Overflow), .Result(Result[7]),
    .Set(one_bit_alu_5_set));
  One_Bit_ALU one_bit_alu_6 (
    .A(A[0]), .B(B[0]), .Less(one_bit_alu_5_set), .Ainvert(Operation[3]), .Binvert(Operation[2]),
    .CarryIn(Operation[2]), .Operation(Operation[1:0]), .CarryOut(one_bit_alu_6_carryout), .Result(Result[0]));  // open: Set
  One_Bit_ALU one_bit_alu_7 (
    .A(A[1]), .B(B[1]), .Less(1'b0), .Ainvert(Operation[3]), .Binvert(Operation[2]),
    .CarryIn(one_bit_alu_6_carryout), .Operation(Operation[1:0]), .CarryOut(one_bit_alu_7_carryout),
    .Result(Result[1]));  // open: Set
  One_Bit_ALU one_bit_alu_8 (
    .A(A[2]), .B(B[2]), .Less(1'b0), .Ainvert(Operation[3]), .Binvert(Operation[2]),
    .CarryIn(one_bit_alu_7_carryout), .Operation(Operation[1:0]), .CarryOut(one_bit_alu_8_carryout),
    .Result(Result[2]));  // open: Set
  or or_1 (or_1_out, Result[0], Result[1], Result[2], Result[3], Result[4], Result[5], Result[6], Result[7]);
  not not_1 (Zero, or_1_out);
endmodule

module One_Bit_ALU (
  input  Ainvert,
  input  Binvert,
  input  CarryIn,
  input  [1:0] Operation,
  input  A,
  input  B,
  input  Less,
  output Result,
  output Set,
  output CarryOut
);

  wire and_1_out, multiplexer_1_out, multiplexer_2_out, not_1_out, not_2_out, or_1_out;

  not not_1 (not_1_out, A);
  Multiplexer #(.enable("false")) multiplexer_1 (.in0(A), .in1(not_1_out), .out(multiplexer_1_out), .sel(Ainvert));
  Multiplexer #(.enable("false")) multiplexer_2 (.in0(B), .in1(not_2_out), .out(multiplexer_2_out), .sel(Binvert));
  not not_2 (not_2_out, B);
  and and_1 (and_1_out, multiplexer_1_out, multiplexer_2_out);
  or or_1 (or_1_out, multiplexer_1_out, multiplexer_2_out);
  Adder #(.width(1)) adder_1 (.a(multiplexer_1_out), .b(multiplexer_2_out), .out(Set), .cin(CarryIn), .cout(CarryOut));
  Multiplexer #(.select(2), .enable("false")) multiplexer_3 (
    .in0(and_1_out), .in1(or_1_out), .in2(Set), .in3(Less), .out(Result), .sel(Operation));
endmodule

module main (
  input  [3:0] Operation,
  input  [7:0] A,
  input  [7:0] B,
  output [7:0] Result,
  output Zero,
  output Overflow
);

  Multi_Bit_ALU multi_bit_alu_1 (
    .A(A), .B(B), .Operation(Operation), .Result(Result), .Zero(Zero), .Overflow(Overflow));

  // Notes on the sheet:
  //   00 - AND
  //   01 - OR
  //   10 - ADD
  //   11 - SUB
endmodule
