// Logisim project register02.circ as structural Verilog: 5 circuits, main circuit main
module main (
  input  [4:0] in_1
);

  Decoder #(.select(5)) decoder_1 (.sel(in_1));  // open: out0, out1, out2, out3, out4, out5, out6, out7, out8, out9, out10, out11, out12, out13, out14, out15, out16, out17, out18, out19, out20, out21, out22, out23, out24, out25, out26, out27, out28, out29, out30, out31, en
endmodule

module SR_Latch (
  input  R,
  input  S,
  output Q
);

  wire nor_2_out;

  nor nor_1 (Q, R, nor_2_out);
  nor nor_2 (nor_2_out, Q, S);
endmodule

module D_Latch (
  input  C,
  input  D,
  output Q
);

  wire and_1_out, and_2_out, nor_2_out, not_1_out;

  not not_1 (not_1_out, D);
  and and_1 (and_1_out, C, not_1_out);
  and and_2 (and_2_out, C, D);
  nor nor_1 (Q, and_1_out, nor_2_out);
  nor nor_2 (nor_2_out, Q, and_2_out);
endmodule

module D_Flipflop (
  input  C,
  input  D,
  output Q
);

  wire and_1_out, and_2_out, and_3_out, and_4_out, nor_1_out, nor_2_out, nor_4_out, not_1_out, not_2_out,
       not_3_out;

  and and_1 (and_1_out, C, not_1_out);
  not not_1 (not_1_out, D);
  and and_2 (and_2_out, C, D);
  not not_2 (not_2_out, C);
  nor nor_1 (nor_1_out, and_1_out, nor_2_out);
  nor nor_2 (nor_2_out, nor_1_out, and_2_out);
  not not_3 (not_3_out, nor_1_out);
  and and_3 (and_3_out, not_2_out, not_3_out);
  and and_4 (and_4_out, not_2_out, nor_1_out);
  nor nor_3 (Q, and_3_out, nor_4_out);
  nor nor_4 (nor_4_out, Q, and_4_out);
endmodule

module Two_Registers (
  input  rd,
  input  rs,
  input  Data,
  input  Clock,
  input  WriteReg,
  input  rt,
  output Q,
  output Q_2
);

  wire and_1_out, and_2_out, and_3_out, and_4_out, and_5_out, and_6_out, and_7_out, and_8_out, and_9_out,
       and_10_out, and_11_out, decoder_1_out0, decoder_1_out1, nor_1_out, nor_2_out, nor_3_out, nor_4_out,
       nor_5_out, nor_6_out, nor_7_out, nor_8_out, not_1_out, not_2_out, not_3_out, not_4_out, not_5_out,
       not_6_out;

  Decoder decoder_1 (.out0(decoder_1_out0), .out1(decoder_1_out1), .sel(rd));  // open: en
  and and_1 (and_1_out, decoder_1_out0, and_3_out);
  and and_2 (and_2_out, decoder_1_out1, and_3_out);
  and and_3 (and_3_out, Clock, WriteReg);
  not not_1 (not_1_out, Data);
  not not_2 (not_2_out, Data);
  not not_3 (not_3_out, and_1_out);
  and and_4 (and_4_out, and_1_out, not_1_out);
  nor nor_1 (nor_1_out, and_4_out, nor_2_out);
  nor nor_2 (nor_2_out, nor_1_out, and_5_out);
  and and_5 (and_5_out, and_1_out, Data);
  not not_4 (not_4_out, and_2_out);
  and and_6 (and_6_out, and_2_out, not_2_out);
  nor nor_3 (nor_3_out, and_6_out, nor_4_out);
  nor nor_4 (nor_4_out, nor_3_out, and_7_out);
  and and_7 (and_7_out, and_2_out, Data);
  not not_5 (not_5_out, nor_1_out);
  not not_6 (not_6_out, nor_3_out);
  and and_8 (and_8_out, not_3_out, not_5_out);
  and and_9 (and_9_out, not_3_out, nor_1_out);
  and and_10 (and_10_out, not_4_out, not_6_out);
  and and_11 (and_11_out, not_4_out, nor_3_out);
  nor nor_5 (nor_5_out, and_8_out, nor_6_out);
  nor nor_6 (nor_6_out, nor_5_out, and_9_out);
  nor nor_7 (nor_7_out, and_10_out, nor_8_out);
  nor nor_8 (nor_8_out, nor_7_out, and_11_out);
  Multiplexer #(.enable("false")) multiplexer_1 (.in0(nor_5_out), .in1(nor_7_out), .out(Q), .sel(rs));
  Multiplexer #(.enable("false")) multiplexer_2 (.in0(nor_5_out), .in1(nor_7_out), .out(Q_2), .sel(rt));
endmodule
