// Logisim project Register.circ as structural Verilog: 4 circuits, main circuit main
module main (
);

  wire clock_1_out;

  Clock clock_1 (.out(clock_1_out));
  // also tied to GND on the sheet: clock_1_out
endmodule

module SR_Latch (
  input  R,
  input  S,
  output Q
);

  wire nor_2_out;

  nor nor_1 (Q, R, nor_2_out);
  nor nor_2 (nor_2_out, Q, S);
endmodule

module D_Latch (
  input  C,
  input  D,
  output Q
);

  wire and_1_out, and_2_out, nor_2_out, not_1_out;

  not not_1 (not_1_out, D);
  and and_1 (and_1_out, C, not_1_out);
  and and_2 (and_2_out, C, D);
  nor nor_1 (Q, and_1_out, nor_2_out);
  nor nor_2 (nor_2_out, Q, and_2_out);
endmodule

module D_FlipFlop (
  input  in_1
);

  wire adder_1_out, and_1_out, and_2_out, and_3_out, and_4_out, nor_1_out, nor_2_out, nor_3_out, nor_4_out,
       not_1_out, not_2_out, not_3_out;

  not not_1 (not_1_out, in_1);
  not not_2 (not_2_out, adder_1_out);
  and and_1 (and_1_out, in_1, not_2_out);
  and and_2 (and_2_out, in_1, adder_1_out);
  nor nor_1 (nor_1_out, and_1_out, nor_2_out);
  nor nor_2 (nor_2_out, nor_1_out, and_2_out);
  not not_3 (not_3_out, nor_1_out);
  and and_3 (and_3_out, not_1_out, not_3_out);
  and and_4 (and_4_out, not_1_out, nor_1_out);
  nor nor_3 (nor_3_out, and_3_out, nor_4_out);
  nor nor_4 (nor_4_out, nor_3_out, and_4_out);
  Adder #(.width(1)) adder_1 (.a(nor_3_out), .b(1'b1), .out(adder_1_out));  // open: cin, cout
endmodule
