// Logisim project muldiv.circ as structural Verilog: 3 circuits, main circuit main
module main (
  input  [15:0] Operand_1__Multiplicand_or_Dividend,
  input  [15:0] Operand_2__Multiplier_and_Divisor,
  input  Mul,
  input  Div,
  output [31:0] Product,
  output M_Ready,
  output [15:0] Quotient,
  output [15:0] Remainder,
  output D_Ready
);

  wire Clock_out;

  // Probe on Operand_1__Multiplicand_or_Dividend
  // Probe on Operand_2__Multiplier_and_Divisor
  _16_bit_Multiplication u_16_bit_multiplication_1 (
    .Multiplicand(Operand_1__Multiplicand_or_Dividend), .Multiplier(Operand_2__Multiplier_and_Divisor),
    .Mul(Mul), .Clock(Clock_out), .Product(Product), .M_Ready(M_Ready));
  _16_bit_Division u_16_bit_division_1 (
    .Divisor(Operand_2__Multiplier_and_Divisor), .Dividend(Operand_1__Multiplicand_or_Dividend), .Div(Div),
    .Clock(Clock_out), .Quotient(Quotient), .Remainder(Remainder), .D_Ready(D_Ready));
  Clock Clock (.out(Clock_out));
  // Probe on Product
  // Probe on Quotient
  // Probe on Remainder
endmodule

module _16_bit_Multiplication (
  input  [15:0] Multiplicand,
  input  [15:0] Multiplier,
  input  Mul,
  input  Clock,
  output [31:0] Product,
  output M_Ready
);

  wire and_2_out, Clear, CLK;
  wire [7:0] counter_1_q, rom_1_data;
  wire [15:0] multiplexer_3_out, Multiplier_2_q, shifter_2_out;
  wire [31:0] adder_1_out, multiplexer_1_out, multiplexer_2_out, Multiplicand_2_q, shifter_1_out;

  // Probe on Multiplicand
  // Probe on Multiplier
  Counter #(.max('h16), .ongoal("stay")) counter_1 (
    .Q(counter_1_q), .carry(M_Ready), .clk(CLK), .clr(Clear));  // open: load, D, count
  not not_1 (Clear, Mul);
  and and_1 (CLK, Mul, Clock);
  ROM rom_1 (.addr(counter_1_q), .data(rom_1_data));  // open: sel
  Multiplexer #(.width(32), .enable("false")) multiplexer_1 (
    .in0({{16{1'b0}}, Multiplicand}), .in1(shifter_1_out), .out(multiplexer_1_out), .sel(rom_1_data[0]));
  Register #(.width(32)) Multiplicand_2 (.D(multiplexer_1_out), .Q(Multiplicand_2_q), .clk(CLK));  // open: en, clr
  Multiplexer #(.width(32), .enable("false")) multiplexer_2 (
    .in0({32{1'b0}}), .in1(Multiplicand_2_q), .out(multiplexer_2_out), .sel(Multiplier_2_q[0]));
  Adder #(.width(32)) adder_1 (.a(Product), .b(multiplexer_2_out), .out(adder_1_out));  // open: cin, cout
  Register #(.width(32)) u_Product (.D(adder_1_out), .Q(Product), .clk(and_2_out), .clr(Clear));  // open: en
  and and_2 (and_2_out, rom_1_data[1], CLK);
  Shifter #(.width(32)) shifter_1 (.in(Multiplicand_2_q), .\dist (5'b00001), .out(shifter_1_out));
  Register #(.width(16)) Multiplier_2 (.D(multiplexer_3_out), .Q(Multiplier_2_q), .clk(CLK));  // open: en, clr
  Multiplexer #(.width(16), .enable("false")) multiplexer_3 (
    .in0(Multiplier), .in1(shifter_2_out), .out(multiplexer_3_out), .sel(rom_1_data[0]));
  // Probe on Product
  Shifter #(.width(16), .shift("lr")) shifter_2 (.in(Multiplier_2_q), .\dist (4'b0001), .out(shifter_2_out));

  // Notes on the sheet:
  //   contents of rom_1 (hex, n*v repeats v):
  //   0 1 3 1 3 1 3 1 3 1 3 1 3 1 3 1 3 1 3 1 3 1 3
  //   Clock to Registers
endmodule

module _16_bit_Division (
  input  [15:0] Divisor,
  input  [15:0] Dividend,
  input  Div,
  input  Clock,
  output [15:0] Quotient,
  output [15:0] Remainder,
  output D_Ready
);

  wire \and , and_2_out, and_3_out, and_4_out, CLK, Clr, comparator_1_eq, comparator_1_gt, comparator_1_lt,
       not_2_out, or_1_out;
  wire [4:0] multiplexer_6_out;
  wire [7:0] counter_1_q, rom_1_data;
  wire [31:0] adder_2_out, Divisor_q, multiplexer_1_out, multiplexer_2_out, multiplexer_3_out,
       multiplexer_4_out, multiplexer_5_out, multiplexer_7_out, shifter_1_out, shifter_2_out,
       subtractor_1_out, Sum;
  wire [31:16] Quotient_q, Remainder_q;

  // Probe on Divisor
  // Probe on Dividend
  ROM rom_1 (.addr(counter_1_q), .data({rom_1_data[7:3], \and , rom_1_data[1:0]}));  // open: sel
  Counter #(.max('h23), .ongoal("stay")) counter_1 (
    .Q(counter_1_q), .carry(D_Ready), .clk(CLK), .clr(Clr));  // open: load, D, count
  not not_1 (Clr, Div);
  and and_1 (CLK, Div, Clock);
  Multiplexer #(.width(32), .enable("false")) multiplexer_1 (
    .in0({Divisor, {16{1'b0}}}), .in1(multiplexer_3_out), .out(multiplexer_1_out), .sel(rom_1_data[0]));
  Multiplexer #(.width(32), .enable("false")) multiplexer_2 (
    .in0({{16{1'b0}}, Dividend}), .in1({Remainder_q, Remainder}), .out(multiplexer_2_out), .sel(rom_1_data[0]));
  Register #(.width(32)) u_Divisor (.D(multiplexer_1_out), .Q(Divisor_q), .clk(CLK));  // open: en, clr
  Multiplexer #(.width(32), .enable("false")) multiplexer_3 (
    .in0(shifter_1_out), .in1(Divisor_q), .out(multiplexer_3_out), .sel(rom_1_data[1]));
  Subtractor #(.width(32)) subtractor_1 (
    .a({Remainder_q, Remainder}), .b(Divisor_q), .out(subtractor_1_out));  // open: bin, bout
  Multiplexer #(.width(32), .enable("false")) multiplexer_4 (
    .in0(multiplexer_2_out), .in1(Sum), .out(multiplexer_4_out), .sel(comparator_1_lt));
  and and_2 (and_2_out, not_2_out, CLK);
  not not_2 (not_2_out, rom_1_data[1]);
  Shifter #(.width(32), .shift("lr")) shifter_1 (.in(Divisor_q), .\dist (5'b00001), .out(shifter_1_out));
  Multiplexer #(.width(32), .enable("false")) multiplexer_5 (
    .in0(multiplexer_4_out), .in1(subtractor_1_out), .out(multiplexer_5_out), .sel(rom_1_data[1]));
  Register #(.width(32)) u_Remainder (
    .D(multiplexer_5_out), .Q({Remainder_q, Remainder}), .clk(and_2_out), .clr(Clr));  // open: en
  Register #(.width(32)) u_Quotient (
    .D(adder_2_out), .Q({Quotient_q, Quotient}), .clk(and_3_out), .clr(Clr));  // open: en
  and and_3 (and_3_out, \and , CLK);
  or or_1 (or_1_out, comparator_1_gt, comparator_1_eq);
  Comparator #(.width(32)) comparator_1 (
    .a({Remainder_q, Remainder}), .b({32{1'b0}}), .gt(comparator_1_gt), .eq(comparator_1_eq),
    .lt(comparator_1_lt));
  Shifter #(.width(32)) shifter_2 (.in({Quotient_q, Quotient}), .\dist (multiplexer_6_out), .out(shifter_2_out));
  Multiplexer #(.width(5), .enable("false")) multiplexer_6 (
    .in0({5{1'b0}}), .in1(5'b00001), .out(multiplexer_6_out), .sel(rom_1_data[1]));
  Multiplexer #(.width(32), .enable("false")) multiplexer_7 (
    .in0({32{1'b0}}), .in1(32'h1), .out(multiplexer_7_out), .sel(and_4_out));
  and and_4 (and_4_out, \and , or_1_out);
  Adder #(.width(32)) adder_1 (.a(Divisor_q), .b({Remainder_q, Remainder}), .out(Sum));  // open: cin, cout
  Adder #(.width(32)) adder_2 (.a(shifter_2_out), .b(multiplexer_7_out), .out(adder_2_out));  // open: cin, cout
  // Probe on Quotient
  // Probe on Remainder

  // Notes on the sheet:
  //   contents of rom_1 (hex, n*v repeats v):
  //   0 3 5 3 5 3 5 3 5 3 5 3 5 3 5 3 5 3 5 3 5 3 5 3 5 3 5 3 5 3 5 3 5 3 5 3 5 3 5 3 5 3 5 3 5 3 5 3 5 3
  //   5 3 5 3 5 3 5 3 5 3 5 3 5
  //   Clock to Registers
endmodule
