// Logisim project lab06.circ as structural Verilog
module One_Bit_Adder (
  input  A,
  input  C_in,
  input  B,
  output Result,
  output Carry_Out
);

  wire and_1_out, and_2_out, and_3_out, and_4_out, and_5_out, and_6_out, and_7_out, and_8_out, and_9_out,
       and_10_out, and_11_out, not_1_out, not_2_out, not_3_out, or_1_out, or_2_out, or_3_out;

  not not_1 (not_1_out, B);
  not not_2 (not_2_out, A);
  not not_3 (not_3_out, C_in);
  and and_1 (and_1_out, not_2_out, not_1_out);
  and and_2 (and_2_out, and_1_out, C_in);
  and and_3 (and_3_out, not_2_out, B);
  and and_4 (and_4_out, and_3_out, not_3_out);
  and and_5 (and_5_out, A, not_1_out);
  and and_6 (and_6_out, and_5_out, not_3_out);
  and and_7 (and_7_out, A, B);
  and and_8 (and_8_out, and_7_out, C_in);
  and and_9 (and_9_out, A, B);
  and and_10 (and_10_out, A, C_in);
  and and_11 (and_11_out, B, C_in);
  or or_1 (or_1_out, and_2_out, and_4_out);
  or or_2 (or_2_out, and_6_out, and_8_out);
  or or_3 (or_3_out, and_9_out, and_10_out);
  or or_4 (Result, or_1_out, or_2_out);
  or or_5 (Carry_Out, or_3_out, and_11_out);
endmodule

module Four_Bit_Adder (
  input  [3:0] A,
  input  [3:0] Result,
  input  [3:0] B
);

  wire one_bit_adder_1_carry_out, one_bit_adder_2_carry_out, one_bit_adder_3_carry_out;

  One_Bit_Adder one_bit_adder_1 (
    .A(A[0]), .B(B[0]), .C_in(1'b0), .Carry_Out(one_bit_adder_1_carry_out), .Result(Result[0]));
  One_Bit_Adder one_bit_adder_2 (
    .A(A[1]), .B(B[1]), .C_in(one_bit_adder_1_carry_out), .Carry_Out(one_bit_adder_2_carry_out),
    .Result(Result[1]));
  One_Bit_Adder one_bit_adder_3 (
    .A(A[2]), .B(B[2]), .C_in(one_bit_adder_2_carry_out), .Carry_Out(one_bit_adder_3_carry_out),
    .Result(Result[2]));
  One_Bit_Adder one_bit_adder_4 (
    .A(A[3]), .B(B[3]), .C_in(one_bit_adder_3_carry_out), .Result(Result[3]));  // open: Carry_Out
endmodule

module Adder_Subtractor (
  input  [7:0] in_1,
  input  [7:0] in_2,
  input  OP,
  output [7:0] Adder_Probe,
  output [7:0] Result,
  output [7:0] Subtractor_Probe
);

  Adder adder_1 (.a(in_1), .b(in_2), .out(Adder_Probe), .cin(1'b0));  // open: cout
  Subtractor subtractor_1 (.a(in_1), .b(in_2), .out(Subtractor_Probe), .bin(1'b0));  // open: bout
  Multiplexer #(.width(8), .enable("false")) multiplexer_1 (
    .in0(Adder_Probe), .in1(Subtractor_Probe), .out(Result), .sel(OP));
endmodule
