// Logisim project muldiv (1).circ as structural Verilog: 3 circuits, main circuit main
module main (
  input  [15:0] Operand_1__Multiplicand_or_Dividend,
  input  [15:0] Operand_2__Multiplier_and_Divisor,
  input  Mul,
  input  Div,
  input  [15:0] Operand_1__Multiplicand_or_Dividend_2,
  input  [15:0] Operand_2__Multiplier_and_Divisor_2,
  input  Div_2,
  output [31:0] Product,
  output M_Ready,
  output [15:0] Quotient,
  output [15:0] Remainder,
  output D_Ready
);

  wire Clock_2_out, Clock_out;

  _16_bit_Multiplication _16_Bit_Multiplication (
    .Multiplicand(Operand_1__Multiplicand_or_Dividend), .Multiplier(Operand_2__Multiplier_and_Divisor),
    .Mul(Mul), .Clock(Clock_out), .M_Ready(M_Ready), .Product(Product));
  Clock Clock (.out(Clock_out));
  _16_bit_Division _16_Bit_Division (
    .Dividend(Operand_1__Multiplicand_or_Dividend_2), .Divisor(Operand_2__Multiplier_and_Divisor_2),
    .Div(Div_2), .Clock(Clock_2_out), .Quotient(Quotient), .Remainder(Remainder), .D_Ready(D_Ready));  // open: D_Ready_2
  Clock Clock_2 (.out(Clock_2_out));
endmodule

module _16_bit_Multiplication (
  input  [15:0] Multiplicand,
  input  [15:0] Multiplier,
  input  Mul,
  input  Clock,
  output M_Ready,
  output [31:0] Product
);

  wire and_1_out, and_2_out, not_1_out, not_2_out;
  wire [7:0] counter_1_q, rom_1_data;
  wire [15:0] multiplexer_1_out, Multiplier_q, shifter_1_out;
  wire [31:0] adder_1_out, bit_extender_1_out, multiplexer_2_out, multiplexer_3_out, Multiplicand_q,
       shifter_2_out;

  Counter #(.max('h1f), .ongoal("stay")) counter_1 (
    .Q(counter_1_q), .carry(M_Ready), .clk(and_1_out), .clr(not_1_out));  // open: load, D, count
  not not_1 (not_1_out, Mul);
  and and_1 (and_1_out, Mul, Clock);
  assign bit_extender_1_out = {{16{1'b0}}, Multiplicand};  // Bit_Extender bit_extender_1
  Multiplexer #(.width(16), .enable("false")) multiplexer_1 (
    .in0(Multiplier), .in1(shifter_1_out), .out(multiplexer_1_out), .sel(rom_1_data[0]));
  ROM rom_1 (.addr(counter_1_q), .data(rom_1_data));  // open: sel
  Multiplexer #(.width(32), .enable("false")) multiplexer_2 (
    .in0(bit_extender_1_out), .in1(shifter_2_out), .out(multiplexer_2_out), .sel(rom_1_data[0]));
  Register #(.width(32)) u_Multiplicand (
    .D(multiplexer_2_out), .en(1'b1), .Q(Multiplicand_q), .clk(and_1_out), .clr(not_2_out));
  Register #(.width(16)) u_Multiplier (.D(multiplexer_1_out), .Q(Multiplier_q), .clk(and_1_out));  // open: en, clr
  Shifter #(.width(16), .shift("lr")) shifter_1 (.in(Multiplier_q), .\dist (4'b0001), .out(shifter_1_out));
  Shifter #(.width(32)) shifter_2 (.in(Multiplicand_q), .\dist (5'b00001), .out(shifter_2_out));
  Multiplexer #(.width(32), .enable("false")) multiplexer_3 (
    .in0({32{1'b0}}), .in1(Multiplicand_q), .out(multiplexer_3_out), .sel(Multiplier_q[0]));
  Adder #(.width(32)) adder_1 (.a(multiplexer_3_out), .b(Product), .out(adder_1_out));  // open: cin, cout
  and and_2 (and_2_out, and_1_out, rom_1_data[1]);
  Register #(.width(32)) u_Product (.D(adder_1_out), .Q(Product), .clk(and_2_out), .clr(not_2_out));  // open: en
  not not_2 (not_2_out, Mul);

  // Notes on the sheet:
  //   contents of rom_1 (hex, n*v repeats v):
  //   24 3 7 23 3 7 23 3 7 23 3 7 23 3 7 23 3 7 23 3 7 23
  //   Clock to Registers
endmodule

module _16_bit_Division (
  input  [15:0] Dividend,
  input  [15:0] Divisor,
  input  Div,
  input  Clock,
  output [15:0] Quotient,
  output [15:0] Remainder,
  output D_Ready,
  output [31:0] D_Ready_2
);

  wire and_1_out, and_2_out, and_3_out, comparator_1_eq, comparator_1_gt, comparator_1_lt, not_1_out,
       not_2_out, not_3_out, or_1_out;
  wire [4:0] multiplexer_6_out;
  wire [7:0] counter_1_q, rom_1_data;
  wire [31:0] adder_1_out, bit_extender_1_out, bit_extender_2_out, Divisor_q, multiplexer_1_out,
       multiplexer_2_out, multiplexer_3_out, multiplexer_4_out, multiplexer_5_out, multiplexer_7_out,
       shifter_1_out, shifter_2_out, shifter_3_out, subtractor_1_out;
  wire [31:16] Quotient_q, Remainder_q;

  ROM rom_1 (.addr(counter_1_q), .data(rom_1_data));  // open: sel
  Counter #(.max('h33), .ongoal("stay")) counter_1 (
    .Q(counter_1_q), .carry(D_Ready), .clk(and_1_out), .clr(not_1_out));  // open: load, D, count
  not not_1 (not_1_out, Div);
  and and_1 (and_1_out, Div, Clock);
  assign bit_extender_1_out = {{16{1'b0}}, Dividend};  // Bit_Extender bit_extender_1
  Multiplexer #(.width(32), .enable("false")) multiplexer_1 (
    .in0(bit_extender_1_out), .in1({Remainder_q, Remainder}), .out(multiplexer_1_out), .sel(rom_1_data[3]));
  not not_2 (not_2_out, D_Ready);
  assign bit_extender_2_out = {{16{1'b0}}, Divisor};  // Bit_Extender bit_extender_2
  Adder #(.width(32)) adder_1 (.a(Divisor_q), .b({Remainder_q, Remainder}), .out(adder_1_out));  // open: cin, cout
  Multiplexer #(.width(32), .enable("false")) multiplexer_2 (
    .in0(multiplexer_1_out), .in1(adder_1_out), .out(multiplexer_2_out), .sel(comparator_1_lt));
  Shifter #(.width(32)) shifter_1 (.in(bit_extender_2_out), .\dist (5'b10000), .out(shifter_1_out));
  Multiplexer #(.width(32), .enable("false")) multiplexer_3 (
    .in0(multiplexer_2_out), .in1(subtractor_1_out), .out(multiplexer_3_out), .sel(rom_1_data[0]));
  Multiplexer #(.width(32), .enable("false")) multiplexer_4 (
    .in0(Divisor_q), .in1(shifter_2_out), .out(multiplexer_4_out), .sel(rom_1_data[2]));
  Multiplexer #(.width(32), .enable("false")) multiplexer_5 (
    .in0(shifter_1_out), .in1(multiplexer_4_out), .out(multiplexer_5_out), .sel(rom_1_data[1]));
  Multiplexer #(.width(5)) multiplexer_6 (
    .in0({5{1'b0}}), .in1(5'b00001), .out(multiplexer_6_out), .sel(rom_1_data[4]));  // open: en
  Register #(.width(32)) u_Divisor (.D(multiplexer_5_out), .Q(Divisor_q), .clk(and_1_out));  // open: en, clr
  Register #(.width(32)) u_Remainder (
    .D(multiplexer_3_out), .Q({Remainder_q, Remainder}), .clk(and_1_out), .clr(not_3_out));  // open: en
  not not_3 (not_3_out, Div);
  and and_2 (and_2_out, rom_1_data[4], and_1_out);
  Shifter #(.width(32), .shift("lr")) shifter_2 (.in(Divisor_q), .\dist (5'b00001), .out(shifter_2_out));
  Register #(.width(32)) u_Quotient (
    .D(D_Ready_2), .Q({Quotient_q, Quotient}), .clk(and_2_out), .clr(not_1_out));  // open: en
  Multiplexer #(.width(32), .enable("false")) multiplexer_7 (
    .in0({32{1'b0}}), .in1(32'h1), .out(multiplexer_7_out), .sel(and_3_out));
  Subtractor #(.width(32)) subtractor_1 (
    .a({Remainder_q, Remainder}), .b(Divisor_q), .out(subtractor_1_out));  // open: bin, bout
  Shifter #(.width(32)) shifter_3 (.in({Quotient_q, Quotient}), .\dist (multiplexer_6_out), .out(shifter_3_out));
  Adder #(.width(32)) adder_2 (.a(shifter_3_out), .b(multiplexer_7_out), .out(D_Ready_2));  // open: cin, cout
  Comparator #(.width(32)) comparator_1 (
    .a({Remainder_q, Remainder}), .b({32{1'b0}}), .gt(comparator_1_gt), .eq(comparator_1_eq),
    .lt(comparator_1_lt));
  or or_1 (or_1_out, comparator_1_gt, comparator_1_eq);
  and and_3 (and_3_out, or_1_out, rom_1_data[4]);

  // Notes on the sheet:
  //   contents of rom_1 (hex, n*v repeats v):
  //   0 b 1a e b 1a e b 1a e b 1a e b 1a e b 1a e b 1a e b 1a e b 1a e b 1a e b 1a e b 1a e b 1a e b 1a e
  //   b 1a e b 1a e b 1a e b 1a e b 1a e b 1a e b 1a e
  //   Clock to Registers
endmodule
